# Fritzing sketch atm_fritzing (saved by Fritzing 0.9.3b)
breadboards: 1

parts:
  Arduino_Uno = Arduino Uno (Rev3)
  RFID = RFID-RC522-v2
  Motor10 = DC Motor
  Motor20 = DC Motor
  Motor50 = DC Motor
  Green_LED = LED - 5mm [color="Red (633nm)" package="5 mm [THT]"]
  Red_LED = LED - 5mm [color="Red (633nm)" package="5 mm [THT]"]
  Weerstand = Resistor [tolerance=±5% resistance=220 package=THT]
  Weerstand_2 = Resistor [tolerance=±5% resistance=220 package=THT]
  Keypad4x4 = Keypad Membran 4x4
  Relay2 = KY-019 5V Relay Module [package="Breakout board"]
  Relay3 = KY-019 5V Relay Module [package="Breakout board"]
  Relay1 = KY-019 5V Relay Module [package="Breakout board"]
  VCC1 = Battery block 9V
  VCC2 = Battery block 9V
  VCC3 = Battery block 9V

nets:
  N1: Arduino_Uno.A0, Keypad4x4.Pin4
  N2: Arduino_Uno.A1, Keypad4x4.Pin3
  N3: Arduino_Uno.A2, Keypad4x4.Pin5
  N4: Arduino_Uno.A3, Keypad4x4.Pin6
  N5: Arduino_Uno.A4/SDA, Keypad4x4.Pin7
  N6: Arduino_Uno.A5/SCL, Keypad4x4.Pin8
  N7: Arduino_Uno.D8, Relay3.S
  N8: Arduino_Uno.D9_PWM, RFID.GND
  N9: Arduino_Uno.D10_PWM/SS, RFID.SDA
  N10: Arduino_Uno.D11_PWM/MOSI, RFID.MOSI
  N11: Arduino_Uno.D12/MISO, RFID.MISO
  N12: Arduino_Uno.D13/SCK, RFID.SCK
  N13: Arduino_Uno.GND, RFID.RST, Weerstand.Pin_0, Weerstand_2.Pin_0, Relay2.-, Relay3.-, Relay1.-
  N14: Arduino_Uno.D2, Relay1.S
  N15: Arduino_Uno.D3_PWM, Keypad4x4.Pin2
  N16: Arduino_Uno.D4, Keypad4x4.Pin1
  N17: Arduino_Uno.D5_PWM, Relay2.S
  N18: Arduino_Uno.D6_PWM, Red_LED.anode
  N19: Arduino_Uno.D7, Green_LED.anode
  3V3: Arduino_Uno.3V3, RFID.3.3V
  N20: Arduino_Uno.5V, Relay2.+, Relay3.+, Relay1.+
  N21: Motor10.pin_1, Relay1.NO
  N22: Motor10.pin_2, VCC1.+
  N23: Motor20.pin_1, Relay2.NO
  N24: Motor20.pin_2, VCC2.+
  N25: Motor50.pin_1, Relay3.NO
  N26: Motor50.pin_2, VCC3.+
  N27: Green_LED.cathode, Weerstand_2.Pin_1
  N28: Red_LED.cathode, Weerstand.Pin_1
  N29: Relay2.Common, VCC2.-
  N30: Relay3.Common, VCC3.-
  N31: Relay1.Common, VCC1.-

custom parts:
  RFID-RC522-v2: A simple China made RFID-RC522 Reader; do check the pin labels, as this is a MFRC522 based clone.
  Keypad Membran 4x4: Membrane Keypad 4x4 Matrix
  KY-019 5V Relay Module: KY-019 5V Relay module, used to control AC circuits.
